# Fritzing sketch PocketBeagle-examples1 (saved by Fritzing 0.9.3b)
breadboards: 1

parts:
  Part1 = PocketBeagle
  Part3 = LED Sequin - Royal Blue [part_number=1757]
  Part4 = Adafruit Micro USB Breakout [part_number="Adafruit #1833"]
  R1 = TRIMPOT [package=trimpot_pth_s3_lock]
  J1 = Basic Servo
  S2 = SWITCH-MOMENTARY-2 [package=tactile-pth-12mm]

nets:
  N1: Part1.USB1.VBUS, Part1.USB1.VIN, Part4.VBUS
  N2: Part1.USB1.DN, Part4.D-
  N3: Part1.USB1.DP, Part4.D+
  N4: Part1.USB1.ID, Part4.ID
  GND: Part1.GND, Part3.-, Part4.GND, J1.gnd
  N5: Part1.AIN.VREFN, R1.CCW
  N6: Part1.AIN.VREFP, R1.CW
  N7: Part1.AIN0(1.8V), R1.WIPER
  N8: Part1.VOUT, J1.vcc
  N9: Part1.PWM0A, Part3.+
  N10: Part1.PWM1A, J1.pulse
  N11: Part1.GPIO23, S2.1
  N12: Part1.3.3V, S2.2

custom parts:
  PocketBeagle: PocketBeagle® is an ultra-tiny-yet-complete Linux-enabled, community-supported, open-source USB-key-fob computer. PocketBeagle features an incredible low cost, slick design and simple usage, making PocketBeagle® the ideal development board for beginners and professionals alike. You develop directly in a web browser and PocketBeagle® can easily be set back to factory conditions, leaving you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
  LED Sequin - Royal Blue: Sew a little sparkle into your wearable project with an Adafruit LED Sequin. Simply connect 3 to 6VDC to the + pin and ground to the - pin, and the LED on the board will light up. You can make the LEDs fade and twinkle by using PWM.
  Adafruit Micro USB Breakout: Simple but effective - this breakout board has a USB Micro-B connector, with all 5 pins broken out. Great for pairing with a microcontroller with USB support, or adding USB 5V power to a project. We use a micro-AB connector with through-hole shielding pads for an excellent strong connection - it won't rip off by accident! Comes with one fully assembled and tested micro B breakout PCB and a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
